// Logisim project logisim74.circ as structural Verilog: 14 circuits, main circuit main
module main (
  input  in_1,
  input  in_2,
  input  in_3,
  input  in_4
);

  wire D_FF_p5;

  // Probe on D_FF_p5
  // DIP_7474 D_FF: pin names not known; wires that end beside it: in_1, in_2, in_3, in_4, D_FF_p5
endmodule

module PC74 (
  input  P2,
  input  [7:0] BUS_in,
  input  Reset_P1,
  input  P1,
  output [15:0] Bus_out
);

  wire AND_p3, clock_1_out, not_1_out, not_2_out, not_3_out, OR_p3, OR_p6;
  wire [7:0] AND_2_p3, buffer_1_out, buffer_2_out, D_FF_2_p2, MUX_p4, XOR_p6;
  wire [7:1] XOR_p8;

  Clock clock_1 (.out(clock_1_out));
  // DIP_7408 AND: pin names not known; wires that end beside it: P2, clock_1_out, AND_p3
  not not_1 (not_1_out, AND_p3);
  not not_2 (not_2_out, Reset_P1);
  // DIP_7432 OR: pin names not known; wires that end beside it: Reset_P1, P1, OR_p3, OR_p3, clock_1_out, OR_p6
  not not_3 (not_3_out, OR_p6);
  // DIP_7486 XOR: pin names not known; wires that end beside it: Bus_out[7], clock_1_out, XOR_p8[7], Bus_out[0], XOR_p6[7], XOR_p6[0], Bus_out[6], XOR_p8[1], XOR_p8[6], Bus_out[1], XOR_p6[6], XOR_p6[1]
  // DIP_7474 D_FF: pin names not known; wires that end beside it: 1'b1, BUS_in[0], not_1_out, 1'b1, Bus_out[8], 1'b1, 1'b1, BUS_in[1], not_1_out, Bus_out[9]
  // DIP_7408 AND_2: pin names not known; wires that end beside it: BUS_in[0], not_2_out, AND_2_p3[0], BUS_in[1], not_2_out, AND_2_p3[1], BUS_in[3], not_2_out, AND_2_p3[3], BUS_in[2], not_2_out, AND_2_p3[2]
  // DIP_7474 D_FF_2: pin names not known; wires that end beside it: 1'b1, D_FF_2_p2[0], not_3_out, 1'b1, Bus_out[0], 1'b1, 1'b1, D_FF_2_p2[1], not_3_out, Bus_out[1]
  // DIP_7486 XOR_2: pin names not known; wires that end beside it: Bus_out[5], XOR_p8[2], XOR_p8[5], Bus_out[2], XOR_p6[5], XOR_p6[2], Bus_out[4], XOR_p8[3], XOR_p8[4], Bus_out[3], XOR_p6[4], XOR_p6[3]
  // DIP_7408 AND_3: pin names not known; wires that end beside it: Bus_out[7], Bus_out[0], XOR_p8[7], clock_1_out, XOR_p8[1], Bus_out[6], Bus_out[1], XOR_p8[6], XOR_p8[1], XOR_p8[7], XOR_p8[2]
  // DIP_7474 D_FF_3: pin names not known; wires that end beside it: 1'b1, D_FF_2_p2[2], not_3_out, 1'b1, Bus_out[2], 1'b1, D_FF_2_p2[3], not_3_out, Bus_out[3]
  // DIP_7474 D_FF_4: pin names not known; wires that end beside it: 1'b1, BUS_in[2], not_1_out, 1'b1, Bus_out[10], 1'b1, 1'b1, BUS_in[3], not_1_out, Bus_out[11]
  // DIP_7408 AND_4: pin names not known; wires that end beside it: BUS_in[4], not_2_out, AND_2_p3[4], BUS_in[5], not_2_out, AND_2_p3[5], BUS_in[7], not_2_out, AND_2_p3[7], BUS_in[6], not_2_out, AND_2_p3[6]
  // DIP_7474 D_FF_5: pin names not known; wires that end beside it: 1'b1, BUS_in[4], not_1_out, 1'b1, Bus_out[12], 1'b1, 1'b1, BUS_in[5], not_1_out, Bus_out[13]
  // DIP_7408 AND_5: pin names not known; wires that end beside it: Bus_out[5], Bus_out[2], XOR_p8[5], XOR_p8[2], XOR_p8[6], XOR_p8[3], Bus_out[4], Bus_out[3], XOR_p8[4], XOR_p8[3], XOR_p8[5], XOR_p8[4]
  // DIP_7474 D_FF_6: pin names not known; wires that end beside it: 1'b1, D_FF_2_p2[4], not_3_out, 1'b1, Bus_out[4], 1'b1, 1'b1, D_FF_2_p2[5], not_3_out, Bus_out[5]
  // DIP_7474 D_FF_7: pin names not known; wires that end beside it: 1'b1, D_FF_2_p2[6], not_3_out, 1'b1, Bus_out[6], 1'b1, 1'b1, D_FF_2_p2[7], not_3_out, Bus_out[7]
  // DIP_7474 D_FF_8: pin names not known; wires that end beside it: 1'b1, BUS_in[6], not_1_out, 1'b1, Bus_out[14], 1'b1, 1'b1, BUS_in[7], not_1_out, Bus_out[15]
  // DIP_74157 MUX: pin names not known; wires that end beside it: clock_1_out, AND_2_p3[0], XOR_p6[0], MUX_p4[0], AND_2_p3[1], XOR_p6[1], 1'b0, AND_2_p3[7], XOR_p6[7], MUX_p4[7], AND_2_p3[6]
  // DIP_74157 MUX_2: pin names not known; wires that end beside it: MUX_p4[1], clock_1_out, AND_2_p3[2], XOR_p6[2], MUX_p4[2], AND_2_p3[3], XOR_p6[3], MUX_p4[3], XOR_p6[6], MUX_p4[6], 1'b0, AND_2_p3[5], XOR_p6[5], MUX_p4[5], AND_2_p3[4], XOR_p6[4], MUX_p4[4]
  assign buffer_1_out = MUX_p4;  // Buffer buffer_1, 8 bits wide
  assign buffer_2_out = buffer_1_out;  // Buffer buffer_2, 8 bits wide
  assign D_FF_2_p2 = buffer_2_out;  // Buffer buffer_3, 8 bits wide
endmodule

module ALU74 (
  input  [7:0] A,
  input  [7:0] B,
  input  [3:0] CU,
  output Garry,
  output Zero,
  output [7:0] Bus
);

  wire ADD_carry, CMPZERO_is_zero;
  wire [7:0] ADD_summe, AND_out_3, mux_1_output_accu, OR_out_3, SHL_output_acc, SHR_output_acc, XOR_out_3;

  ADD74 ADD (.SUB_A(CU[1]), .B(B), .SUMME(ADD_summe), .CARRY(ADD_carry), .A(A), .SUB_B(CU[0]));
  AND74 AND (.A(A), .B(B), .out_3(AND_out_3));
  OR74 OR (.A(A), .B(B), .out_3(OR_out_3));
  XOR74 XOR (.A(A), .B(B), .out_3(XOR_out_3));
  SHL74 SHL (.B(B), .A(A), .Output_Acc(SHL_output_acc));
  SHR74 SHR (.B(B), .A(A), .Output_Acc(SHR_output_acc));
  MUX mux_1 (
    .ADD(ADD_summe), .SUB(ADD_summe), .AND(AND_out_3), .OR(OR_out_3), .XOR(XOR_out_3), .SHL(SHL_output_acc),
    .SHR(SHR_output_acc), .A(A), .Output_Accu(mux_1_output_accu), .CU(CU[2:0]));
  // Probe on SHR_output_acc
  // Probe on SHL_output_acc
  // Probe on XOR_out_3
  // Probe on OR_out_3
  // Probe on AND_out_3
  // Probe on ADD_summe
  CMPZERO74 CMPZERO (.Input(mux_1_output_accu), .is_zero(CMPZERO_is_zero));
  // DIP_7486 XOR_3: pin names not known; wires that end beside it: CMPZERO_is_zero, CU[3], CU[3], ADD_carry, Zero, Garry
  INV74 INV (.Input(mux_1_output_accu), .Output(Bus), .INV(CU[3]));
  // Probe on mux_1_output_accu
endmodule

module AND74 (
  input  [7:0] A,
  input  [7:0] B,
  output [7:0] out_3
);

  // DIP_7408 AND: pin names not known; wires that end beside it: B[7], B[3], A[7], A[3], out_3[7], out_3[3], B[6], B[2], A[6]
  // DIP_7408 AND_2: pin names not known; wires that end beside it: A[2], out_3[6], out_3[2], B[5], B[1], A[5], A[1], out_3[5], out_3[1], B[4], B[0], A[4], A[0], out_3[4], out_3[0]
endmodule

module OR74 (
  input  [7:0] A,
  input  [7:0] B,
  output [7:0] out_3
);

  // DIP_7432 OR: pin names not known; wires that end beside it: B[7], B[3], A[7], A[3], out_3[7], out_3[3], B[6], B[2], A[6]
  // DIP_7432 OR_2: pin names not known; wires that end beside it: A[2], out_3[6], out_3[2], B[5], B[1], A[5], A[1], out_3[5], out_3[1], B[4], B[0], A[4], A[0], out_3[4], out_3[0]
endmodule

module XOR74 (
  input  [7:0] A,
  input  [7:0] B,
  output [7:0] out_3
);

  // DIP_7486 XOR: pin names not known; wires that end beside it: B[7], B[3], A[7], A[3], out_3[7], out_3[3], B[6], B[2], A[6]
  // DIP_7486 XOR_2: pin names not known; wires that end beside it: A[2], out_3[6], out_3[2], B[5], B[1], A[5], A[1], out_3[5], out_3[1], B[4], B[0], A[4], A[0], out_3[4], out_3[0]
endmodule

module ADD74 (
  input  SUB_A,
  input  SUB_B,
  input  [7:0] A,
  input  [7:0] B,
  output [7:0] SUMME,
  output CARRY
);

  wire OR_p5, XOR_9_p7;
  wire [7:0] AND_4_p14, AND_4_p15, XOR_4_p15, XOR_6_p14, XOR_8_p11, XOR_p5;

  // DIP_7486 XOR: pin names not known; wires that end beside it: A[0], SUB_B, SUB_A, B[7], XOR_p5[0], XOR_4_p15[7], A[1], SUB_B, SUB_A
  // DIP_7486 XOR_2: pin names not known; wires that end beside it: B[6], XOR_p5[1], XOR_4_p15[6], A[2], SUB_B, SUB_A, B[5], XOR_p5[2], XOR_4_p15[5], A[3], SUB_B, SUB_A
  // DIP_7486 XOR_3: pin names not known; wires that end beside it: B[4], XOR_p5[3], XOR_4_p15[4], A[4], SUB_B, SUB_A, B[3], XOR_p5[4], XOR_4_p15[3], A[5], SUB_B, SUB_A
  // DIP_7486 XOR_4: pin names not known; wires that end beside it: B[2], XOR_p5[5], XOR_4_p15[2], A[6], SUB_B, SUB_A, B[1], XOR_p5[6], XOR_4_p15[1], SUB_A, SUB_B, A[7], B[0], XOR_p5[7], XOR_4_p15[0]
  // DIP_7486 XOR_5: pin names not known; wires that end beside it: XOR_p5[3], XOR_p5[4], XOR_4_p15[3], XOR_4_p15[4], XOR_6_p14[3], XOR_6_p14[4], XOR_p5[2], XOR_p5[5], XOR_4_p15[2]
  // DIP_7486 XOR_6: pin names not known; wires that end beside it: XOR_4_p15[5], XOR_6_p14[2], XOR_6_p14[5], XOR_p5[1], XOR_p5[6], XOR_4_p15[1], XOR_4_p15[6], XOR_6_p14[1], XOR_6_p14[6], XOR_p5[0], XOR_p5[7], XOR_4_p15[0], XOR_4_p15[7], XOR_6_p14[0], XOR_6_p14[7]
  // DIP_7408 AND: pin names not known; wires that end beside it: XOR_8_p11[7], XOR_p5[7], XOR_6_p14[7], XOR_4_p15[7], AND_4_p14[7], AND_4_p15[7], XOR_8_p11[6], XOR_p5[6], XOR_6_p14[6]
  // DIP_7408 AND_2: pin names not known; wires that end beside it: XOR_4_p15[6], AND_4_p14[6], AND_4_p15[6], XOR_8_p11[5], XOR_p5[5], XOR_6_p14[5], XOR_4_p15[5], AND_4_p14[5], AND_4_p15[5], XOR_8_p11[4], XOR_p5[4], XOR_6_p14[4]
  // DIP_7408 AND_3: pin names not known; wires that end beside it: XOR_4_p15[4], AND_4_p14[4], AND_4_p15[4], XOR_8_p11[3], XOR_p5[3], XOR_6_p14[3], XOR_4_p15[3], AND_4_p14[3], AND_4_p15[3], XOR_8_p11[2], XOR_p5[2], XOR_6_p14[2]
  // DIP_7486 XOR_7: pin names not known; wires that end beside it: XOR_8_p11[7], XOR_8_p11[3], XOR_6_p14[7], XOR_6_p14[3], SUMME[7], SUMME[3], XOR_8_p11[6], XOR_8_p11[2], XOR_6_p14[6]
  // DIP_7486 XOR_8: pin names not known; wires that end beside it: XOR_6_p14[2], SUMME[6], SUMME[2], XOR_8_p11[5], XOR_8_p11[1], XOR_6_p14[5], XOR_6_p14[1], SUMME[5], SUMME[1], XOR_8_p11[4], XOR_8_p11[0], XOR_6_p14[4], XOR_6_p14[0], SUMME[4], SUMME[0]
  // DIP_7408 AND_4: pin names not known; wires that end beside it: XOR_4_p15[2], AND_4_p14[2], AND_4_p15[2], XOR_8_p11[1], XOR_p5[1], XOR_6_p14[1], XOR_4_p15[1], AND_4_p14[1], AND_4_p15[1], XOR_8_p11[0], XOR_p5[0], XOR_6_p14[0], XOR_4_p15[0], AND_4_p14[0], AND_4_p15[0]
  // DIP_7432 OR: pin names not known; wires that end beside it: AND_4_p14[7], AND_4_p14[3], AND_4_p15[7], AND_4_p15[3], OR_p5, XOR_8_p11[4], AND_4_p14[6], AND_4_p14[2], AND_4_p15[6]
  // DIP_7486 XOR_9: pin names not known; wires that end beside it: SUB_B, SUB_A, XOR_8_p11[0], SUB_B, OR_p5, SUB_A, XOR_9_p7, XOR_9_p7, CARRY
  // DIP_7432 OR_2: pin names not known; wires that end beside it: AND_4_p15[2], XOR_8_p11[7], XOR_8_p11[3], AND_4_p14[5], AND_4_p14[1], AND_4_p15[5], AND_4_p15[1], XOR_8_p11[6], XOR_8_p11[2], AND_4_p14[4], AND_4_p14[0], AND_4_p15[4], AND_4_p15[0], XOR_8_p11[5], XOR_8_p11[1]

  // Notes on the sheet:
  //   CARRY
endmodule

module SHL74 (
  input  [7:0] A,
  input  [7:0] B,
  output [7:0] Output_Acc
);

  wire AND_2_p6, AND_2_p7, AND_2_p12, AND_2_p13, AND_p3, AND_p9, MUX_8_in_2_p5, MUX_8_in_p5, NOT_p3, OR_p3,
       OR_p4, OR_p5, OR_p6;

  // DIP_7432 OR: pin names not known; wires that end beside it: B[7], B[5], OR_p3, OR_p4, OR_p5, OR_p6, B[6], B[4], OR_p6, B[3], OR_p4
  // DIP_7404 NOT: pin names not known; wires that end beside it: OR_p3, OR_p5, NOT_p3
  // DIP_74151 MUX_8_in: pin names not known; wires that end beside it: 1'b0, 1'b0, 1'b0, A[0], MUX_8_in_p5, 1'b0, 1'b0, 1'b0, 1'b0, 1'b0, B[0], B[1], B[2]
  // DIP_7408 AND: pin names not known; wires that end beside it: NOT_p3, NOT_p3, AND_p3, MUX_8_in_p5, Output_Acc[4], Output_Acc[0], NOT_p3, NOT_p3, AND_p9
  // DIP_74151 MUX_8_in_2: pin names not known; wires that end beside it: 1'b0, 1'b0, A[0], A[1], MUX_8_in_2_p5, 1'b0, 1'b0, 1'b0, 1'b0, 1'b0, B[0], B[1], B[2]
  // DIP_7408 AND_2: pin names not known; wires that end beside it: MUX_8_in_2_p5, Output_Acc[5], Output_Acc[1], NOT_p3, NOT_p3, AND_2_p6, AND_2_p7, Output_Acc[6], Output_Acc[2], NOT_p3, NOT_p3, AND_2_p12, AND_2_p13, Output_Acc[7], Output_Acc[3]
  // DIP_74151 MUX_8_in_3: pin names not known; wires that end beside it: 1'b0, A[0], A[1], A[2], AND_2_p7, 1'b0, 1'b0, 1'b0, 1'b0, 1'b0, B[0], B[1], B[2]
  // DIP_74151 MUX_8_in_4: pin names not known; wires that end beside it: A[0], A[1], A[2], A[3], AND_2_p13, 1'b0, 1'b0, 1'b0, 1'b0, 1'b0, B[0], B[1], B[2]
  // DIP_74151 MUX_8_in_5: pin names not known; wires that end beside it: A[1], A[2], A[3], A[4], AND_p3, 1'b0, A[0], 1'b0, 1'b0, 1'b0, B[0], B[1], B[2]
  // DIP_74151 MUX_8_in_6: pin names not known; wires that end beside it: A[2], A[3], A[4], A[5], AND_p9, 1'b0, A[1], A[0], 1'b0, 1'b0, B[0], B[1], B[2]
  // DIP_74151 MUX_8_in_7: pin names not known; wires that end beside it: A[3], A[4], A[5], A[6], AND_2_p6, 1'b0, A[2], A[1], A[0], 1'b0, B[0], B[1], B[2]
  // DIP_74151 MUX_8_in_8: pin names not known; wires that end beside it: A[4], A[5], A[6], A[7], AND_2_p12, 1'b0, A[3], A[2], A[1], A[0], B[0], B[1], B[2]
endmodule

module SHR74 (
  input  [7:0] A,
  input  [7:0] B,
  output [7:0] Output_Acc
);

  wire AND_2_p6, AND_2_p7, AND_2_p12, AND_2_p13, AND_p3, AND_p9, MUX_8_in_2_p5, MUX_8_in_p5, NOT_p3, OR_p3,
       OR_p4, OR_p5, OR_p6;

  // DIP_7432 OR: pin names not known; wires that end beside it: B[7], B[5], OR_p3, OR_p4, OR_p5, OR_p6, B[6], B[4], OR_p6, B[3], OR_p4
  // DIP_7404 NOT: pin names not known; wires that end beside it: OR_p3, OR_p5, NOT_p3
  // DIP_74151 MUX_8_in: pin names not known; wires that end beside it: 1'b0, 1'b0, 1'b0, A[7], MUX_8_in_p5, 1'b0, 1'b0, 1'b0, 1'b0, 1'b0, B[0], B[1], B[2]
  // DIP_7408 AND: pin names not known; wires that end beside it: NOT_p3, NOT_p3, AND_p3, MUX_8_in_p5, Output_Acc[3], Output_Acc[7], NOT_p3, NOT_p3, AND_p9
  // DIP_74151 MUX_8_in_2: pin names not known; wires that end beside it: 1'b0, 1'b0, A[7], A[6], MUX_8_in_2_p5, 1'b0, 1'b0, 1'b0, 1'b0, 1'b0, B[0], B[1], B[2]
  // DIP_7408 AND_2: pin names not known; wires that end beside it: MUX_8_in_2_p5, Output_Acc[2], Output_Acc[6], NOT_p3, NOT_p3, AND_2_p6, AND_2_p7, Output_Acc[1], Output_Acc[5], NOT_p3, NOT_p3, AND_2_p12, AND_2_p13, Output_Acc[0], Output_Acc[4]
  // DIP_74151 MUX_8_in_3: pin names not known; wires that end beside it: 1'b0, A[7], A[6], A[5], AND_2_p7, 1'b0, 1'b0, 1'b0, 1'b0, 1'b0, B[0], B[1], B[2]
  // DIP_74151 MUX_8_in_4: pin names not known; wires that end beside it: A[7], A[6], A[5], A[4], AND_2_p13, 1'b0, 1'b0, 1'b0, 1'b0, 1'b0, B[0], B[1], B[2]
  // DIP_74151 MUX_8_in_5: pin names not known; wires that end beside it: A[6], A[5], A[4], A[3], AND_p3, 1'b0, A[7], 1'b0, 1'b0, 1'b0, B[0], B[1], B[2]
  // DIP_74151 MUX_8_in_6: pin names not known; wires that end beside it: A[5], A[4], A[3], A[2], AND_p9, 1'b0, A[6], A[7], 1'b0, 1'b0, B[0], B[1], B[2]
  // DIP_74151 MUX_8_in_7: pin names not known; wires that end beside it: A[4], A[3], A[2], A[1], AND_2_p6, 1'b0, A[5], A[6], A[7], 1'b0, B[0], B[1], B[2]
  // DIP_74151 MUX_8_in_8: pin names not known; wires that end beside it: A[3], A[2], A[1], A[0], AND_2_p12, 1'b0, A[4], A[5], A[6], A[7], B[0], B[1], B[2]
endmodule

module INV74 (
  input  [7:0] Input,
  input  INV,
  output [7:0] Output
);

  wire [7:0] bit_extender_1_out;

  assign bit_extender_1_out = {{7{INV}}, INV};  // Bit_Extender bit_extender_1
  // DIP_7486 XOR: pin names not known; wires that end beside it: bit_extender_1_out[7], bit_extender_1_out[4], Input[7], Input[3], Output[7], Output[3], bit_extender_1_out[6], bit_extender_1_out[5], Input[6], Input[2], Output[6], Output[2]
  // DIP_7486 XOR_2: pin names not known; wires that end beside it: bit_extender_1_out[1], bit_extender_1_out[2], Input[5], Input[1], Output[5], Output[1], bit_extender_1_out[0], bit_extender_1_out[3], Input[4], Input[0], Output[4], Output[0]
endmodule

module CMPZERO74 (
  input  [7:0] Input,
  output is_zero
);

  wire OR_2_p1, OR_2_p2, OR_2_p7, OR_2_p8, OR_p3, OR_p4, OR_p5;

  // DIP_7432 OR: pin names not known; wires that end beside it: Input[5], Input[4], OR_p3, OR_p4, OR_p5, OR_p3, OR_p5, Input[3], Input[6]
  // DIP_7432 OR_2: pin names not known; wires that end beside it: OR_2_p1, OR_2_p2, OR_p4, OR_2_p2, Input[2], Input[7], OR_2_p7, OR_2_p8, OR_2_p1, Input[1]
  // DIP_7404 NOT: pin names not known; wires that end beside it: Input[0], OR_2_p7, OR_2_p8, is_zero
endmodule

module MUX (
  input  [7:0] ADD,
  input  [2:0] CU,
  input  [7:0] SUB,
  input  [7:0] AND,
  input  [7:0] OR,
  input  [7:0] XOR,
  input  [7:0] SHL,
  input  [7:0] SHR,
  input  [7:0] A,
  output [7:0] Output_Accu
);

  Mux2bit MUX_Modul (
    ._8_Bit_input_1({A[0], SHR[0], SHL[0], XOR[0], OR[0], AND[0], SUB[0], ADD[0]}), .Bit_2(Output_Accu[1]),
    .Bit_1(Output_Accu[0]), .CU(CU),
    ._8_Bit_input_1_2({A[1], SHR[1], SHL[1], XOR[1], OR[1], AND[1], SUB[1], ADD[1]}));
  Mux2bit MUX_Modul_2 (
    ._8_Bit_input_1({A[2], SHR[2], SHL[2], XOR[2], OR[2], AND[2], SUB[2], ADD[2]}), .Bit_2(Output_Accu[3]),
    .Bit_1(Output_Accu[2]), .CU(CU),
    ._8_Bit_input_1_2({A[3], SHR[3], SHL[3], XOR[3], OR[3], AND[3], SUB[3], ADD[3]}));
  Mux2bit MUX_Modul_3 (
    ._8_Bit_input_1({A[4], SHR[4], SHL[4], XOR[4], OR[4], AND[4], SUB[4], ADD[4]}), .Bit_2(Output_Accu[5]),
    .Bit_1(Output_Accu[4]), .CU(CU),
    ._8_Bit_input_1_2({A[5], SHR[5], SHL[5], XOR[5], OR[5], AND[5], SUB[5], ADD[5]}));
  Mux2bit MUX_Modul_4 (
    ._8_Bit_input_1({A[6], SHR[6], SHL[6], XOR[6], OR[6], AND[6], SUB[6], ADD[6]}), .Bit_2(Output_Accu[7]),
    .Bit_1(Output_Accu[6]), .CU(CU),
    ._8_Bit_input_1_2({A[7], SHR[7], SHL[7], XOR[7], OR[7], AND[7], SUB[7], ADD[7]}));
endmodule

module Mux2bit (
  input  [2:0] CU,
  input  [7:0] _8_Bit_input_1,
  input  [7:0] _8_Bit_input_1_2,
  output Bit_1,
  output Bit_2
);

  // DIP_74151 dip_74151_1: pin names not known; wires that end beside it: _8_Bit_input_1[3], _8_Bit_input_1[2], _8_Bit_input_1[1], _8_Bit_input_1[0], Bit_1, 1'b0, _8_Bit_input_1[4], _8_Bit_input_1[5], _8_Bit_input_1[6], _8_Bit_input_1[7], CU[0], CU[1], CU[2]
  // DIP_74151 dip_74151_2: pin names not known; wires that end beside it: _8_Bit_input_1_2[3], _8_Bit_input_1_2[2], _8_Bit_input_1_2[1], _8_Bit_input_1_2[0], Bit_2, 1'b0, _8_Bit_input_1_2[4], _8_Bit_input_1_2[5], _8_Bit_input_1_2[6], _8_Bit_input_1_2[7], CU[0], CU[1], CU[2]
endmodule

module test (
  input  in_1,
  input  in_2,
  input  in_3,
  input  in_4
);

  wire dip_7474_1_p5;

  // DIP_7474 dip_7474_1: pin names not known; wires that end beside it: in_2, in_4, in_3, in_2, dip_7474_1_p5, in_1
endmodule
